# Fritzing sketch Untitled Sketch (saved by Fritzing 0.9.3b)
breadboards: 1

parts:
  元件1 = OLED Monochrome 128x64 0.96 inch [part_number=326]
  元件2 = Arduino Uno (Rev3)
  LED1 = LED - 5mm [color="Red (633nm)" package="5 mm [THT]"]
  LED2 = LED - 5mm [color="Red (633nm)" package="5 mm [THT]"]
  LED3 = LED - 5mm [color="Red (633nm)" package="5 mm [THT]"]
  LED4 = LED - 5mm [color="Red (633nm)" package="5 mm [THT]"]
  LED5 = LED - 5mm [color="Red (633nm)" package="5 mm [THT]"]
  LED6 = LED - 5mm [color="Red (633nm)" package="5 mm [THT]"]
  LED7 = LED - 5mm [color="Red (633nm)" package="5 mm [THT]"]
  LED8 = LED - 5mm [color="Red (633nm)" package="5 mm [THT]"]
  J1 = Basic Force Sensing Resistor (FSR) [package=THT]
  R1 = Resistor [tolerance=±5% resistance=220 package=THT]
  R2 = Resistor [tolerance=±5% resistance=220 package=THT]
  R3 = Resistor [tolerance=±5% resistance=220 package=THT]
  R4 = Resistor [tolerance=±5% resistance=220 package=THT]
  R5 = Resistor [tolerance=±5% resistance=220 package=THT]
  R6 = Resistor [tolerance=±5% resistance=220 package=THT]
  R7 = Resistor [tolerance=±5% resistance=220 package=THT]
  R8 = Resistor [tolerance=±5% resistance=220 package=THT]
  R9 = Resistor [tolerance=±5% resistance=220 package=THT]

nets:
  N1: 元件1.MOSI_SDA, 元件2.D11_PWM/MOSI
  N2: 元件1.SCLK_SCK, 元件2.D12/MISO
  N3: 元件1.DC_SA0, 元件2.D9_PWM
  N4: 元件1.RESET, 元件2.D10_PWM/SS
  N5: 元件1.CS, 元件2.D8
  VIN: 元件1.VIN, 元件2.5V, J1.pin_0
  GND: 元件1.GND, 元件2.GND, R1.Pin_1, R2.Pin_1, R3.Pin_1, R4.Pin_1, R5.Pin_1, R6.Pin_1, R7.Pin_1, R8.Pin_1, R9.Pin_1
  N6: 元件2.A0, J1.pin_1, R1.Pin_0
  N7: 元件2.D13/SCK, LED1.anode
  N8: 元件2.D1/TX, LED8.anode
  N9: 元件2.D2, LED7.anode
  N10: 元件2.D3_PWM, LED6.anode
  N11: 元件2.D4, LED5.anode
  N12: 元件2.D5_PWM, LED4.anode
  N13: 元件2.D6_PWM, LED3.anode
  N14: 元件2.D7, LED2.anode
  N15: LED1.cathode, R2.Pin_0
  N16: LED2.cathode, R3.Pin_0
  N17: LED3.cathode, R4.Pin_0
  N18: LED4.cathode, R6.Pin_0
  N19: LED5.cathode, R7.Pin_0
  N20: LED6.cathode, R5.Pin_0
  N21: LED7.cathode, R8.Pin_0
  N22: LED8.cathode, R9.Pin_0

custom parts:
  OLED Monochrome 128x64 0.96 inch: These displays are small, only about 1" diameter, but very readable due to the high contrast of an OLED display. This display is made of 128x64 individual white OLED pixels, each one is turned on or off by the controller chip. Because the display makes its own light, no backlight is required. This reduces the power required to run the OLED and is why the display has such high contrast; we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
